# Fritzing sketch schema (saved by Fritzing 0.9.4)
breadboards: 1

parts:
  U2 = ESP8266 NodeMCU LoLin module
  R2 = Resistor [tolerance=±5% resistance=10k package=THT]
  KY-1 = Keyes Relay [package=THT]
  Power_plug1 = Power plug
  LED1 = LED - 5mm [color="Red (633nm)" package="5 mm [THT]"]

nets:
  N1: U2.D2, R2.Pin_1
  N2: U2.3V3, R2.Pin_0
  N3: KY-1.NC, LED1.cathode
  N4: KY-1.C, Power_plug1.VCC
  N5: Power_plug1.GND, LED1.anode

custom parts:
  ESP8266 NodeMCU LoLin module: ESP8266 based NodeMCU
  Keyes Relay: The Keyes 5V relay module is suitable for SCM development, home appliance control. It uses a 5V~12V TIL control signal which can control DC / AC signal.
